# Fritzing sketch liquid_level (saved by Fritzing 0.9.10b)
breadboards: 1

parts:
  Mod1 = Raspberry Pi 4B
  HC-SR04_Sensor_3 = HC-SR04 Ultrasonic Distance Sensor
  HC-SR04_Sensor_1 = HC-SR04 Ultrasonic Distance Sensor
  HC-SR04_Sensor_2 = HC-SR04 Ultrasonic Distance Sensor
  R1 = Resistor [tolerance=±5% resistance=220 package="2512 [SMD]"]
  R4 = Resistor [tolerance=±5% resistance=330 package="0603 [SMD]"]
  R6 = Resistor [tolerance=±5% resistance=330 package="0603 [SMD]"]
  R8 = Resistor [tolerance=±5% resistance=330 package="0603 [SMD]"]
  R10 = Resistor [tolerance=±5% resistance=220 power=0.5W package="2512 [SMD]"]
  R11 = Resistor [tolerance=±5% resistance=220 package="2512 [SMD]"]

nets:
  VCC: Mod1.5V, HC-SR04_Sensor_3.VCC, HC-SR04_Sensor_1.VCC, HC-SR04_Sensor_2.VCC
  GND: Mod1.GND, HC-SR04_Sensor_3.GND, HC-SR04_Sensor_1.GND, HC-SR04_Sensor_2.GND, R4.Pin_0, R6.Pin_0, R8.Pin_0
  N1: Mod1.GPIO23, HC-SR04_Sensor_1.TRIG
  N2: Mod1.GPIO24, R1.Pin_0, R4.Pin_1
  N3: Mod1.GPIO5, HC-SR04_Sensor_2.TRIG
  N4: Mod1.GPIO6, R6.Pin_1, R10.Pin_0
  N5: Mod1.GPIO16, HC-SR04_Sensor_3.TRIG
  N6: Mod1.GPIO20, R8.Pin_1, R11.Pin_0
  N7: HC-SR04_Sensor_3.ECHO, R11.Pin_1
  N8: HC-SR04_Sensor_1.ECHO, R1.Pin_1
  N9: HC-SR04_Sensor_2.ECHO, R10.Pin_1
