# Fritzing sketch pump_controller (saved by Fritzing 0.9.10b)

parts:
  M1 = DC Motor [voltage_(max)=12V voltage_(min)=3V]
  M2 = DC Motor [voltage_(max)=12V voltage_(min)=3V]
  Mod1 = Raspberry Pi 4B
  VCC1 = Battery block 9V
  M3 = DC Motor [voltage_(max)=12V voltage_(min)=3V]
  Mod2 = L298N DC motor driver
  Mod3 = L298N DC motor driver

nets:
  N1: M1.pin_1, Mod2.OUT1
  N2: M1.pin_2, Mod2.OUT2
  N3: M2.pin_1, Mod3.OUT4
  N4: M2.pin_2, Mod3.OUT3
  5V: Mod1.5V, Mod2.5V, Mod2.+5V-J1, Mod2.+5V-J2, Mod2.ENA, Mod2.ENB, Mod3.5V, Mod3.+5V-J1, Mod3.+5V-J2, Mod3.ENA, Mod3.ENB
  GND: Mod1.GND, VCC1.-, Mod2.GND, Mod3.GND
  N5: Mod1.GPIO14, Mod2.IN1
  N6: Mod1.GPIO15, Mod2.IN2
  N7: Mod1.GPIO18, Mod2.IN3
  N8: Mod1.GPIO27, Mod2.IN4
  N9: Mod1.GPIO8, Mod3.IN3
  N10: Mod1.GPIO7, Mod3.IN4
  12V: VCC1.+, Mod2.12V, Mod2.5V-ENA-JMP-I, Mod2.5V-ENA-JMP-O, Mod3.12V, Mod3.5V-ENA-JMP-I, Mod3.5V-ENA-JMP-O
  N11: M3.pin_1, Mod2.OUT4
  N12: M3.pin_2, Mod2.OUT3

custom parts:
  L298N DC motor driver: 2x DC motor driver with 78M05 positive voltage regulator (7..35 V) L298N: max 46 V, 2 A Set 5 V Enable jumper to enable 5 V regultor (needed for the L298N) and +5 V output at screw terminal or supply external +5 V at screw terminal Set ENA and/or ENB to +5 V to enable motor permanently or supply ENA and/or ENB with PWM signal IN1 and IN2 set rotation directory for motor A (OUT1/OUT2) IN2 and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
