# Fritzing sketch temperature_sense_hat (saved by Fritzing 0.9.10b)
breadboards: 1

parts:
  RPi4_B = Raspberry Pi 4B
  LCD2 = LCD screen
  R1 = Resistor [tolerance=±5% power=0.25 resistance=220 package=THT]
  R2 = Resistor [tolerance=±5% power=0.25 resistance=2.2k package=THT]

nets:
  5V: RPi4_B.5V, LCD2.VDD, R1.Pin_0
  GND: RPi4_B.GND, LCD2.VSS, LCD2.R/W, LCD2.LED-, R2.Pin_0
  N1: RPi4_B.GPIO18, LCD2.RS
  N2: RPi4_B.GPIO23, LCD2.E
  N3: RPi4_B.GPIO24, LCD2.DB7
  N4: RPi4_B.GPIO25, LCD2.DB6
  N5: RPi4_B.GPIO8, LCD2.DB5
  N6: RPi4_B.GPIO7, LCD2.DB4
  N7: LCD2.V0, R2.Pin_1
  N8: LCD2.LED+, R1.Pin_1
